// Logisim project run.circ as structural Verilog: 1 circuit, main circuit main
module main (
  output [15:0] s0_Value,
  output [15:0] s1_Value,
  output [15:0] s2_Value,
  output [15:0] ra_Value,
  output [15:0] sp_Value,
  output [15:0] hi_Value,
  output [15:0] lo_Value,
  output [15:0] Time_Step,
  output [15:0] Requested_Address,
  output [15:0] Requested_Instruction
);

  wire clock_1_out, overflow;

  Clock clock_1 (.out(clock_1_out));
  // cpu_main main_1: pin names not known; wires that end beside it: Requested_Instruction, s0_Value, s1_Value, clock_1_out, s2_Value, ra_Value, sp_Value, hi_Value, lo_Value, overflow, Requested_Address
  Counter #(.width(16), .max('hffff)) counter_1 (.Q(Time_Step), .clk(clock_1_out));  // open: load, D, count, carry, clr
  // Probe on Requested_Address
  ROM #(.addrWidth(14), .dataWidth(16)) rom_1 (
    .addr(Requested_Address[14:1]), .data(Requested_Instruction));  // open: sel
  // Probe on Requested_Instruction

  // Other names for the same wires on the sheet: fetch_addr[15:0] = Requested_Address;
  //   Instruction[15:0] = Requested_Instruction

  // Notes on the sheet:
  //   YOUR CPU SHOULD FIT IN HERE!
  //   Instruction Memory
endmodule
