// Logisim project alu.circ as structural Verilog: 1 circuit, main circuit main
module main (
  input  [15:0] X,
  input  [15:0] Y,
  input  [2:0] Switch,
  output Equal,
  output [15:0] Result,
  output [15:0] or_out,
  output [15:0] Result_2,
  output [15:0] and_out,
  output Signed_Overflow,
  output [15:0] addu_out,
  output [15:0] sll_out,
  output [15:0] srl_out,
  output [15:0] slt_out,
  output [15:0] add_out,
  output add_overflow
);

  wire adder_1_cout, adder_2_cout, lessthan;
  wire [3:0] bit_extender_1_out, bit_extender_2_out;
  wire [15:0] mult_out1, mult_out2;

  Bit_Extender #(.in_width(16), .out_width(4)) bit_extender_1 (.in(Y), .out(bit_extender_1_out));
  Bit_Extender #(.in_width(16), .out_width(4)) bit_extender_2 (.in(Y), .out(bit_extender_2_out));
  Adder #(.width(16)) adder_1 (.a(X), .b(Y), .out(add_out), .cout(adder_1_cout));  // open: cin
  assign or_out = X | Y;  // OR_Gate or_1, 16 bits wide
  assign and_out = X & Y;  // AND_Gate and_1, 16 bits wide
  Shifter #(.width(16)) shifter_1 (.in(X), .\dist (bit_extender_1_out), .out(sll_out));
  Shifter #(.width(16), .shift("lr")) shifter_2 (.in(X), .\dist (bit_extender_2_out), .out(srl_out));
  Adder #(.width(15)) adder_2 (.a(X[14:0]), .b(Y[14:0]), .cout(adder_2_cout));  // open: out, cin
  xor xor_1 (add_overflow, adder_2_cout, adder_1_cout);
  Comparator #(.width(16)) comparator_1 (.a(X), .b(Y), .eq(Equal));  // open: gt, lt
  Adder #(.width(16)) adder_3 (.a(X), .b(Y), .out(addu_out));  // open: cin, cout
  Comparator #(.width(16)) comparator_2 (.a(X), .b(Y), .lt(lessthan));  // open: gt, eq
  Multiplexer #(.width(16), .enable("false")) multiplexer_1 (
    .in0({16{1'b0}}), .in1(16'h1), .out(slt_out), .sel(lessthan));
  Multiplier #(.width(16)) multiplier_1 (.a(X), .b(Y), .out(mult_out1), .cout(mult_out2));  // open: cin
  Multiplexer #(.select(3), .width(16), .enable("false")) multiplexer_2 (
    .in0(sll_out), .in1(srl_out), .in2(add_out), .in3(and_out), .in4(or_out), .in5(addu_out), .in6(slt_out),
    .in7(mult_out1), .out(Result), .sel(Switch));
  Multiplexer #(.select(3), .enable("false")) multiplexer_3 (
    .in0(1'b0), .in1(1'b0), .in2(add_overflow), .in3(1'b0), .in4(1'b0), .in5(1'b0), .in6(1'b0), .in7(1'b0),
    .out(Signed_Overflow), .sel(Switch));
  Multiplexer #(.select(3), .width(16), .enable("false")) multiplexer_4 (
    .in0(sll_out), .in1(srl_out), .in2(add_out), .in3(and_out), .in4(or_out), .in5(addu_out), .in6(slt_out),
    .in7(mult_out2), .out(Result_2), .sel(Switch));

  // Other names for the same wires on the sheet: overflow = Signed_Overflow; S[2:0] = Switch

  // Notes on the sheet:
  //   INPUTS to your circuit
  //   swtich 4 -> or
  //   swtich 0 -> sll 
  //   swtich 1 -> srl 
  //   swtich 2 -> add 
  //   swtich 3 -> and
  //   DON'T CHANGE THE LOCATIONS OF THE INPUTS AND OUTPUTS!
  //   swtich 5 -> addu
  //   swtich 6 -> slt
  //   control of equal
  //   swtich 7 -> mult
  //   OUTPUTS from your circuit
endmodule
