// Logisim project cpu.circ as structural Verilog: 2 circuits, main circuit main
module main (
  input  [15:0] INSTRUCTION,
  input  CLOCK,
  output [15:0] FETCH_ADDRESS,
  output Overflow,
  output [15:0] s0_Value,
  output [15:0] s1_Value,
  output [15:0] s2_Value,
  output [15:0] ra_Value,
  output [15:0] sp_Value,
  output [15:0] HI_Value,
  output [15:0] LO_Value,
  output [15:0] out_12,
  output [15:0] out_13,
  output [15:0] out_14,
  output [1:0] out_15,
  output [2:0] out_16
);

  wire and_1_out, and_2_out, and_3_out, beq, bne, branch, comparator_1_eq, comparator_2_eq, isImm, J, jr,
       lui, main_2_equal, MEM_p1, MEM_p2, MEM_p4, MEM_p9, MEM_p11, MEM_p13, MEM_p15, MemToReg, MemWrite,
       mfhi, mflo, mult, not_1_out, not_2_out, or_1_out, or_2_out, or_3_out, overflow_t, RegDst, RegWrite,
       \signed , sw;
  wire [2:0] funct, multiplexer_1_out, multiplexer_3_out, multiplexer_5_out, multiplexer_12_out,
       multiplexer_14_out, rd, rs, rt;
  wire [3:0] opcode;
  wire [5:0] imm_i;
  wire [9:0] imm_u;
  wire [15:0] adder_1_out, adder_2_out, ALU2, alu_o2, alu_res, bit_extender_1_out, bit_extender_3_out,
       branchAddr, ext, loop, MemOut, multiplexer_4_out, multiplexer_6_out, multiplexer_7_out,
       multiplexer_8_out, multiplexer_9_out, multiplexer_13_out, multiplexer_15_out, multiplexer_17_out,
       multiplexer_18_out, multiplexer_20_out, offset, register_1_q, shifter_1_out;
  wire [15:13] multiplexer_19_out;

  Register #(.width(16)) PC (.D(loop), .Q(FETCH_ADDRESS), .clk(CLOCK));  // open: en, clr
  Multiplexer #(.width(3), .enable("false")) multiplexer_1 (
    .in0(rt), .in1(rd), .out(multiplexer_1_out), .sel(or_1_out));
  or or_1 (or_1_out, beq, sw, bne);
  or or_2 (or_2_out, J, jr);
  Adder #(.width(16)) adder_1 (.a(FETCH_ADDRESS), .b(16'h2), .out(adder_1_out));  // open: cin, cout
  assign bit_extender_1_out = {{10{1'b0}}, imm_i};  // Bit_Extender bit_extender_1
  Multiplexer #(.width(16), .enable("false")) multiplexer_2 (
    .in0(bit_extender_1_out), .in1(offset), .out(ext), .sel(\signed ));
  assign offset = {{10{imm_i[5]}}, imm_i};  // Bit_Extender bit_extender_2
  Adder #(.width(16)) adder_2 (.a(FETCH_ADDRESS), .b(offset), .out(adder_2_out));  // open: cin, cout
  Multiplexer #(.width(3), .enable("false")) multiplexer_3 (.in0(rt), .in1(rd), .out(multiplexer_3_out), .sel(RegDst));
  Multiplexer #(.width(16), .enable("false")) multiplexer_4 (
    .in0(adder_1_out), .in1(FETCH_ADDRESS), .out(multiplexer_4_out), .sel(branch));
  Subtractor #(.width(16)) subtractor_1 (.a(adder_2_out), .b(16'h2), .out(branchAddr));  // open: bin, bout
  Multiplexer #(.width(3), .enable("false")) multiplexer_5 (
    .in0(multiplexer_3_out), .in1(out_16), .out(multiplexer_5_out), .sel(J));
  Multiplexer #(.width(16), .enable("false")) multiplexer_6 (
    .in0(multiplexer_7_out), .in1(FETCH_ADDRESS), .out(multiplexer_6_out), .sel(or_2_out));
  Multiplexer #(.width(16), .enable("false")) multiplexer_7 (
    .in0(alu_res), .in1(MemOut), .out(multiplexer_7_out), .sel(MemToReg));
  Multiplexer #(.width(16), .enable("false")) multiplexer_8 (
    .in0(multiplexer_4_out), .in1(branchAddr), .out(multiplexer_8_out), .sel(branch));
  regfile_main main_1 (
    .Read_Register_1(rs), .Read_Register_2(multiplexer_1_out), .Write_Register(multiplexer_5_out),
    .Write_Data(multiplexer_6_out), .Write_Enable(and_1_out), .Clock(CLOCK), .Read_Data_1(out_14),
    .Read_Data_2(out_13), .s0_Value(s0_Value), .s1_Value(s1_Value), .s2_Value(s2_Value), .ra_Value(ra_Value),
    .sp_Value(sp_Value));
  and and_1 (and_1_out, not_1_out, RegWrite);
  Multiplexer #(.width(16), .enable("false")) multiplexer_9 (
    .in0(multiplexer_8_out), .in1({FETCH_ADDRESS[15:10], imm_u}), .out(multiplexer_9_out), .sel(J));
  Multiplexer #(.width(16), .enable("false")) multiplexer_10 (.in0(out_13), .in1(ext), .out(ALU2), .sel(isImm));
  not not_1 (not_1_out, overflow_t);
  Multiplexer #(.width(16), .enable("false")) multiplexer_11 (
    .in0(multiplexer_9_out), .in1(out_12), .out(loop), .sel(jr));
  // mem_main MEM: pin names not known; wires that end beside it: MEM_p1, MEM_p2, MEM_p2, MEM_p4, out_12, out_13, MemWrite, CLOCK, MEM_p9, MemOut, MEM_p11, MEM_p11, MEM_p13, MEM_p13, MEM_p15
  assign bit_extender_3_out = {{6{1'b0}}, imm_u};  // Bit_Extender bit_extender_3
  Multiplexer #(.select(3), .width(3), .enable("false")) multiplexer_12 (
    .in0(3'b000), .in1(3'b001), .in2(3'b010), .in3(3'b011), .in4(3'b100), .in5(3'b101), .in6(3'b110),
    .in7(3'b111), .out(multiplexer_12_out), .sel(funct));
  Shifter #(.width(16)) shifter_1 (.in(bit_extender_3_out), .\dist (4'b0110), .out(shifter_1_out));
  Multiplexer #(.width(16), .enable("false")) multiplexer_13 (
    .in0(out_12), .in1(HI_Value), .out(multiplexer_13_out), .sel(mfhi));
  Multiplexer #(.select(4), .width(3), .enable("false")) multiplexer_14 (
    .in0(multiplexer_12_out), .in1(3'b000), .in2(3'b000), .in3(3'b010), .in4(3'b000), .in5(3'b000),
    .in6(3'b010), .in7(3'b010), .in8(3'b110), .in9(3'b011), .in10(3'b100), .in11(3'b010), .in12(3'b010),
    .in13(3'b000), .in14(3'b000), .in15(3'b000), .out(multiplexer_14_out), .sel(opcode));
  Multiplexer #(.width(16), .enable("false")) multiplexer_15 (
    .in0(LO_Value), .in1(shifter_1_out), .out(multiplexer_15_out), .sel(lui));
  Multiplexer #(.width(16), .enable("false")) multiplexer_16 (
    .in0(multiplexer_13_out), .in1(LO_Value), .out(alu_res), .sel(mflo));
  Multiplexer #(.width(16), .enable("false")) multiplexer_17 (
    .in0(multiplexer_15_out), .in1(out_12), .out(multiplexer_17_out), .sel(mult));
  or or_3 (or_3_out, J, jr, branch);
  alu_main main_2 (
    .Switch(multiplexer_14_out), .X(out_14), .Equal(main_2_equal), .Result(out_12), .Y(ALU2),
    .Result_2(alu_o2), .Signed_Overflow(overflow_t));  // open: add_overflow, add_out, srl_out, sll_out, and_out, or_out, addu_out, slt_out
  Register #(.width(16)) LO (.D(multiplexer_17_out), .Q(LO_Value), .clk(CLOCK));  // open: en, clr
  Multiplexer #(.width(16), .enable("false")) multiplexer_18 (
    .in0(INSTRUCTION), .in1({16{1'b0}}), .out(multiplexer_18_out), .sel(or_3_out));
  Register #(.width(16)) register_1 (.D(multiplexer_18_out), .Q(register_1_q), .clk(CLOCK));  // open: en, clr
  not not_2 (not_2_out, main_2_equal);
  Multiplexer #(.select(4), .width(16), .enable("false")) multiplexer_19 (
    .in0(16'h9), .in1(16'h82), .in2(16'h48), .in3(16'h41b), .in4(16'h210), .in5(16'h110), .in6(16'h1b),
    .in7(16'h1b), .in8(16'h1b), .in9(16'hb), .in10(16'hb), .in11(16'h1f), .in12(16'h32), .in13(16'h809),
    .in14(16'h1009),
    .out({multiplexer_19_out, mflo, mfhi, jr, beq, bne, lui, J, MemWrite, \signed , RegWrite, MemToReg, isImm, RegDst}),
    .sel(opcode));  // open: in15
  Instruction_Decompose instruction_decompose_1 (
    .Input(register_1_q), .out_2(rt), .out_3(funct), .out_4(rs), .out_5(rd), .out_6(opcode), .out_7(out_15),
    .out_8(imm_i), .out_9(imm_u));
  and and_2 (and_2_out, beq, main_2_equal);
  and and_3 (and_3_out, not_2_out, bne);
  or or_4 (branch, and_2_out, and_3_out);
  Comparator #(.width(3)) comparator_1 (.a(funct), .b(3'b111), .eq(comparator_1_eq));  // open: gt, lt
  Comparator #(.width(4)) comparator_2 (.a(opcode), .b(4'b0000), .eq(comparator_2_eq));  // open: gt, lt
  and and_4 (mult, comparator_1_eq, comparator_2_eq);
  Multiplexer #(.width(16), .enable("false")) multiplexer_20 (
    .in0(HI_Value), .in1(alu_o2), .out(multiplexer_20_out), .sel(mult));
  assign out_16 = {{1{1'b0}}, out_15};  // Bit_Extender bit_extender_4
  Register #(.width(16)) HI (.D(multiplexer_20_out), .Q(HI_Value), .clk(CLOCK));  // open: en, clr
  Comparator #(.width(4)) comparator_3 (.a(opcode), .b(4'b1100), .eq(sw));  // open: gt, lt

  // Other names for the same wires on the sheet: ALU1[15:0] = out_14; alu_o1[15:0] = out_12; clk = CLOCK;
  //   CurrPC[15:0] = FETCH_ADDRESS; fetch_addr[15:0] = FETCH_ADDRESS; hi[15:0] = HI_Value; lo[15:0] = LO_Value;
  //   ra[15:0] = ra_Value; rd_u[1:0] = out_15; rd_u_3[2:0] = out_16; rtval[15:0] = out_13; s0[15:0] = s0_Value;
  //   s1[15:0] = s1_Value; s2[15:0] = s2_Value; signed_overflow = Overflow; sp[15:0] = sp_Value

  // Notes on the sheet:
  //   Output
  //   These are outputs/inputs from run.circ
  //   Inputs
  //   These are DEBUG/TEST outputs from your circuit.
endmodule

module Instruction_Decompose (
  input  [15:0] Input,
  output [2:0] out_2,
  output [2:0] out_3,
  output [2:0] out_4,
  output [2:0] out_5,
  output [3:0] out_6,
  output [1:0] out_7,
  output [5:0] out_8,
  output [9:0] out_9
);


  assign out_2 = Input[5:3];
  assign out_3 = Input[2:0];
  assign out_4 = Input[8:6];
  assign out_5 = Input[11:9];
  assign out_6 = Input[15:12];
  assign out_7 = Input[11:10];
  assign out_8 = Input[5:0];
  assign out_9 = Input[9:0];

  // Other names for the same wires on the sheet: funct[2:0] = Input[2:0]; imm_i[5:0] = Input[5:0];
  //   imm_u[9:0] = Input[9:0]; opcode[3:0] = Input[15:12]; rd[2:0] = Input[11:9]; rd_u[1:0] = Input[11:10];
  //   rs[2:0] = Input[8:6]; rt[2:0] = Input[5:3]
endmodule
